// Logisim project MEM.circ as structural Verilog: 1 circuit, main circuit MEM
module MEM (
  input  [3:0] wd,
  input  [7:0] addr,
  input  mw,
  input  clk,
  input  mr,
  output [3:0] data
);

  wire or_1_out;

  or or_1 (or_1_out, mw, mr);
  RAM #(.dataWidth(4)) ram_1 (.addr(addr), .data(data), .sel(or_1_out), .clk(clk), .ld(mr), .clr(1'b0));
  assign data = mw ? wd : 4'bz;  // Controlled_Buffer controlled_buffer_1
endmodule
