// Logisim project STALL.circ as structural Verilog: 1 circuit, main circuit STALL
module STALL (
  input  [3:0] rdest,
  input  mr,
  input  [3:0] rs,
  input  [3:0] rt,
  output stall
);

  wire and_1_out, and_2_out;
  wire [3:0] xnor_1_out, xnor_2_out;

  assign xnor_1_out = ~(rdest ^ rs);  // XNOR_Gate xnor_1, 4 bits wide
  assign xnor_2_out = ~(rt ^ rdest);  // XNOR_Gate xnor_2, 4 bits wide
  and and_1 (and_1_out, xnor_1_out[0], xnor_1_out[1], xnor_1_out[2], xnor_1_out[3], mr);
  and and_2 (and_2_out, xnor_2_out[0], xnor_2_out[1], xnor_2_out[2], xnor_2_out[3], mr);
  or or_1 (stall, and_1_out, and_2_out);
endmodule
